// Logisim project cpu2.circ as structural Verilog: 22 circuits, main circuit main
module main (
  input  in_1
);

  wire clock_1_out, cpu_1_dev, cpu_1_hlt, cpu_1_int, cpu_1_r_nw, \cpu_1_ø1 , keyboard_1_avail,
       keyboard_2_kclk, not_1_out, not_2_out, terminal_controller_1_clk_term, terminal_controller_1_cls,
       undriven;
  wire [6:0] keyboard_1_data, terminal_controller_1_data_2;
  wire [7:0] cpu_1_memout;
  wire [15:0] cpu_1_ab;
  wire [17:16] cpu_1_ab_2;

  LED HLT (.in(cpu_1_hlt));
  Clock clock_1 (.out(clock_1_out));
  LED KERNEL_MODE (.in(cpu_1_ab_2[17]));
  Keyboard keyboard_1 (.clk(keyboard_2_kclk), .avail(keyboard_1_avail), .data(keyboard_1_data));  // open: re, clr
  CPU cpu_1 (
    .MEMIN(cpu_1_memout), .MEMOUT(cpu_1_memout), .AB({cpu_1_ab_2, cpu_1_ab}), .IRQ(undriven),
    .CLK(clock_1_out), .\Ø1 (\cpu_1_ø1 ), .DEV(cpu_1_dev), .R_nW(cpu_1_r_nw), .INT(cpu_1_int),
    .HLT(cpu_1_hlt), .RES(in_1));  // open: Ø2
  not not_1 (not_1_out, cpu_1_r_nw);
  not not_2 (not_2_out, cpu_1_ab_2[16]);
  KEYBOARD keyboard_2 (
    .CLK(\cpu_1_ø1 ), .DEV(cpu_1_dev), .R_W(cpu_1_r_nw), .ADDRESS(cpu_1_ab[7:0]), .INT(cpu_1_int),
    .DATA_2(cpu_1_memout), .KCLK(keyboard_2_kclk), .BUFFER(keyboard_1_avail), .DATA(keyboard_1_data));  // open: IRQ
  TTY #(.rows(16), .cols(60)) tty_1 (
    .data(terminal_controller_1_data_2), .clk(terminal_controller_1_clk_term), .clr(terminal_controller_1_cls));  // open: we
  Terminal_Controller terminal_controller_1 (
    .Address(cpu_1_ab[7:0]), .R_W(cpu_1_r_nw), .CLK(\cpu_1_ø1 ), .Data(cpu_1_memout),
    .CLK_TERM(terminal_controller_1_clk_term), .DATA_2(terminal_controller_1_data_2), .DEVICE(cpu_1_dev),
    .CLS(terminal_controller_1_cls));
  RAM #(.addrWidth(16)) ram_1 (
    .addr(cpu_1_ab), .data(cpu_1_memout), .sel(not_2_out), .clk(\cpu_1_ø1 ), .ld(not_1_out));  // open: clr
  EXTERNAL_MEMORY external_memory_1 (
    .Q(cpu_1_memout), .D(cpu_1_memout), .CLK(\cpu_1_ø1 ), .DEVICE(cpu_1_dev), .R_W(cpu_1_r_nw),
    .Address(cpu_1_ab[7:0]));
endmodule

module CPU (
  input  [7:0] MEMIN,
  input  CLK,
  input  IRQ,
  input  RES,
  output R_nW,
  output HLT,
  output \Ø1 ,
  output INT,
  output [7:0] MEMOUT,
  output \Ø2 ,
  output DEV,
  output [17:0] AB
);

  wire _0_A, _0_ADH, _0_B, _1_ADH, _1_B, ADC, ADD, ADH_A, ADH_ABH, ADH_KPCH, ADH_PCH, ADH_SB, ADH_UPCH,
       ADL_A, ADL_ABL, ADL_KPCL, ADL_PCL, ADL_SB, ADL_SP, ADL_UPCL, alu_1_cout, alu_1_zero, ALUOP, AND,
       AX_SB, BX_SB, CALLVEC, CLC, CLI, CLK_t, clock_1_out, CLZ, CX_ADL, CX_SB, CYEND, D_IR, DB_A, DB_FR,
       DB_SB, DCX, DIV, DL_ADH, DL_ADL, DL_DB, DL_SB, DSP, DX_SB, fr_1_cf, fr_1_kf, FR_DB, ICX, INT_ADL,
       INTVEC, IPC, ISP, KOR, MUL, nDB_A, NOT, not_1_out, not_2_out, OR, or_1_out, PCH_ADH, PCL_ADL,
       predecode_logic_1_admem, RETVEC, SB_ADH, SB_ADL, SB_AX, SB_B, SB_BX, SB_CX, SB_DB, SB_DX, SB_SP, SBB,
       SEC, SEI, SEK, SEZ, SHL, SHR, SP_ADL, SP_SB, SUB, XOR;
  wire [7:0] a_b_1_a, a_b_1_b, dl_2_out_7, fr_1_fr, gate_1_a_2, gate_2_a_2, pointer_1_adh_2, pointer_1_adl_2,
       pointer_1_sb_2, predecode_logic_1_out_11;
  wire [13:0] predecode_logic_1_inst;
  wire [31:0] R1, R2, R3;

  Pull_Resistor pull_resistor_1 (.node(RES));
  // Probe on predecode_logic_1_out_11
  PREDECODE__LOGIC predecode_logic_1 (
    .IRQ(IRQ), .CLK(\Ø1 ), .DL_IR(D_IR), .RESCYC(CYEND), .FR(fr_1_fr), .DATA(gate_1_a_2),
    .ADMEM(predecode_logic_1_admem), .INST(predecode_logic_1_inst), .out_11(predecode_logic_1_out_11),
    .KOR(KOR), .INT(INT), .RES(not_1_out));
  not not_1 (not_1_out, RES);
  not not_2 (not_2_out, R_nW);
  GATE gate_1 (.B(MEMIN), .B_2(MEMOUT), .A_2(gate_1_a_2), .A(gate_1_a_2), .B_A(not_2_out), .A_B(R_nW));
  assign gate_1_a_2 = R_nW ? gate_2_a_2 : 8'bz;  // Controlled_Buffer controlled_buffer_1
  Clock clock_1 (.out(clock_1_out));
  or or_1 (or_1_out, clock_1_out, CLK);
  ROM #(.addrWidth(14), .dataWidth(32)) rom_1 (.addr(predecode_logic_1_inst), .data(R1));  // open: sel
  ROM #(.addrWidth(14), .dataWidth(32)) rom_2 (.addr(predecode_logic_1_inst), .data(R2));  // open: sel
  ROM #(.addrWidth(14), .dataWidth(32)) rom_3 (.addr(predecode_logic_1_inst), .data(R3));  // open: sel
  and and_1 (\Ø1 , ~HLT, or_1_out);  // AND_Gate
  not not_3 (\Ø2 , \Ø1 );
  POINTER pointer_1 (
    .ADL(pointer_1_adl_2), .ADH(pointer_1_adh_2), .SB(pointer_1_sb_2), .ADL_UPCL(ADL_UPCL),
    .ADH_UPCH(ADH_UPCH), .ADL_KPCL(ADL_KPCL), .ADH_KPCH(ADH_KPCH), .SB_SP(SB_SP), .ADL_SP(ADL_SP),
    .SB_CX(SB_CX), .ADL_2(pointer_1_adl_2), .ADH_2(pointer_1_adh_2), .SB_2(pointer_1_sb_2),
    .PCL_ADH(PCL_ADL), .PCH_ADH(PCH_ADH), .SP_ADL(SP_ADL), .SP_SB(SP_SB), .CX_ADL(CX_ADL), .CX_SB(CX_SB),
    .DCX(DCX), .ICX(ICX), .DSP(DSP), .ISP(ISP), .IPC(IPC), .KF(fr_1_kf), .CLK(\Ø1 ), .ADL_PCL(ADH_PCH),
    .ADH_PCH(ADL_PCL), .RES(not_1_out));
  REGISTER register_1 (
    .SB(pointer_1_sb_2), .SB_AX(SB_AX), .SB_BX(SB_BX), .SB_DX(SB_DX), .out_10(pointer_1_sb_2), .AX_SB(AX_SB),
    .BX_SB(BX_SB), .DX_SB(DX_SB), .CLK(\Ø1 ), .RES(not_1_out));
  // Probe on dl_2_out_7
  GATE gate_2 (.B(pointer_1_sb_2), .B_2(pointer_1_sb_2), .A_2(gate_2_a_2), .A(gate_2_a_2), .B_A(SB_DB), .A_B(DB_SB));
  GATE gate_3 (
    .B(pointer_1_sb_2), .B_2(pointer_1_sb_2), .A_2(pointer_1_adl_2), .A(pointer_1_adl_2), .B_A(SB_ADL),
    .A_B(ADL_SB));
  VECTOR_TABLE vector_table_1 (
    .CALLVEC(CALLVEC), .ADL(pointer_1_adl_2), .ADH(pointer_1_adh_2), .RETVEC(RETVEC), .INTVEC(INTVEC));
  DL dl_2 (
    .DATA(gate_1_a_2), .DL_DB(DL_DB), .DL_ADL(DL_ADL), .DL_ADH(DL_ADH), .DL_SB(DL_SB), .CLK(\Ø2 ),
    .SB(pointer_1_sb_2), .ADL(pointer_1_adl_2), .ADH(pointer_1_adh_2), .DB(gate_2_a_2), .out_7(dl_2_out_7));
  GATE gate_4 (
    .B(pointer_1_sb_2), .B_2(pointer_1_sb_2), .A_2(pointer_1_adh_2), .A(pointer_1_adh_2), .B_A(SB_ADH),
    .A_B(ADH_SB));
  ADDRESS_BUS address_bus_1 (
    ._1_ADH(_1_ADH), ._0_ADH(_0_ADH), .ADL(pointer_1_adl_2), .ADH(pointer_1_adh_2), .ADL_ABL(ADL_ABL),
    .ADH_ABH(ADH_ABH), .AB(AB), .CLK(\Ø1 ), .ADDMEM(predecode_logic_1_admem), .DEVICE(DEV), .KF(fr_1_kf),
    .R_nW(R_nW), .RES(not_1_out));
  A_B a_b_1 (
    .DB(gate_2_a_2), .SB(pointer_1_sb_2), .ADL(pointer_1_adl_2), .ADH(pointer_1_adh_2), .DB_A(DB_A),
    .ADL_A(ADL_A), .ADH_A(ADH_A), .SB_B(SB_B), ._0_B(_0_B), ._1_B(_1_B), .A(a_b_1_a), .B(a_b_1_b),
    .CLK(\Ø1 ), ._0_A(_0_A), .nDB_A(nDB_A), .RES(not_1_out));
  // Probe on AB
  ALU alu_1 (
    .A(a_b_1_a), .B(a_b_1_b), .SB(pointer_1_sb_2), .ADD(ADD), .ADC(ADC), .SUB(SUB), .SBB(SBB), .MUL(MUL),
    .DIV(DIV), .SHL(SHL), .SHR(SHR), .AND(AND), .OR(OR), .XOR(XOR), .NOT(NOT), .CF(fr_1_cf),
    .ZERO(alu_1_zero), .COUT(alu_1_cout));
  FR fr_1 (
    .DB(gate_2_a_2), .DB_2(gate_2_a_2), .FR_DB(FR_DB), .CLZ(CLZ), .SEZ(SEZ), .CLC(CLC), .SEC(SEC),
    .CLK(CLK_t), .SEK(SEK), .CLI(CLI), .SEI(SEI), .CARRY(alu_1_cout), .ZERO(alu_1_zero), .ALUOP(ALUOP),
    .CLK_2(\Ø1 ), .CF(fr_1_cf), .KF(fr_1_kf), .FR(fr_1_fr), .DB_FR(DB_FR), .RES(not_1_out));  // open: ZF, IF
  R1 r1_1 (
    .in_1(R1), .out_2(DL_SB), .out_3(DL_DB), .out_4(AX_SB), .out_5(BX_SB), .out_6(DX_SB), .out_7(SB_DB),
    .out_8(DB_SB), .out_9(SB_CX), .out_10(SB_SP), .out_11(FR_DB), .out_12(SP_SB), .out_13(CX_SB),
    .out_14(SB_AX), .out_15(SB_BX), .out_16(SB_DX), .out_17(SB_B), .out_18(DB_A), .out_19(_0_A),
    .out_20(nDB_A), .out_21(ADL_PCL), .out_22(ADH_PCH), .out_23(INTVEC), .out_24(HLT));  // open: out_25, out_26, out_27, out_28, out_29, out_30, out_31, out_32, out_33
  R1 r1_2 (
    .in_1(R2), .out_2(_1_ADH), .out_3(_0_ADH), .out_4(ADL_ABL), .out_5(ADH_ABH), .out_6(SB_ADL),
    .out_7(ADL_SB), .out_8(SB_ADH), .out_9(ADH_SB), .out_10(ADL_UPCL), .out_11(ADH_UPCH), .out_12(ADL_KPCL),
    .out_13(ADH_KPCH), .out_14(ADL_SP), .out_15(DL_ADL), .out_16(DL_ADH), .out_17(PCL_ADL), .out_18(PCH_ADH),
    .out_19(ADL_A), .out_20(ADH_A), .out_21(INT_ADL), .out_22(SP_ADL), .out_23(CX_ADL), .out_24(DSP),
    .out_25(ISP), .out_26(IPC), .out_27(ICX), .out_28(DCX), .out_29(KOR), .out_30(CALLVEC), .out_31(RETVEC));  // open: out_32, out_33
  R1 r1_3 (
    .in_1(R3), .out_2(ALUOP), .out_3(AND), .out_4(SHL), .out_5(SHR), .out_6(OR), .out_7(XOR), .out_8(NOT),
    .out_9(ADD), .out_10(ADC), .out_11(SUB), .out_12(SBB), .out_13(MUL), .out_14(DIV), .out_15(_0_B),
    .out_16(_1_B), .out_17(CLK_t), .out_18(SEK), .out_19(CLI), .out_20(SEI), .out_21(CLZ), .out_22(SEZ),
    .out_23(CLC), .out_24(SEC), .out_25(DEV), .out_26(R_nW), .out_27(D_IR), .out_28(CYEND), .out_29(DB_FR));  // open: out_30, out_31, out_32, out_33

  // Notes on the sheet:
  //   ADDMEM
  //   contents of rom_1 (hex, n*v repeats v):
  //   242*0 400000 15*0 2004 15*0 84 15*0 4004 15*0 1008 15*0 88 15*0 4008 15*0 1800 15*0 2800 15*0 4800
  //   15*0 1010 15*0 2010 15*0 90 15*0 1400 15*0 2400 15*0 104 15*0 108 271*0 10024 8008 1000 13*0 10024
  //   8008 1000 13*0 10024 8008 1000 13*0 10024 8008 1000 13*0 10024 8008 1000 13*0 10024 8008 1000 13*0
  //   10024 8008 1000 13*0 10024 8008 1000 13*0 10024 8008 1000 13*0 10024 8008 1000 13*0 10024 8008 1000
  //   29*0 10024 1000 14*0 10028 1000 559*0 10002 0 180000 13*0 8800 0 80000 0 100000 203*0 8001 0 40002
  //   20 0 20 0 20000 24*0 24 15*0 28 15*0 820 15*0 30 31*0 200 16*0 1001 15*0 2001 15*0 81 15*0 4001 31*0
  //   2 47*0 30 16*0 4001 13*0 1001 15*0 2001 15*0 81 15*0 4001 15*0 101 15*0 2 178*0 1001 15*0 2001 15*0
  //   81 15*0 4001 15*0 24 15*0 28 15*0 820 15*0 30 15*0 101 15*0 420 15*0 2 15*0 200 27*0 4 8 4001 13*0 4
  //   8 30 31*0 1001 15*0 2001 15*0 81 15*0 4001 15*0 24 15*0 28 15*0 820 15*0 30 15*0 2 15*0 101 15*0 200
  //   15*0 420 78*0 8800 0 1001 13*0 8800 0 2001 13*0 8800 0 24 13*0 8800 0 28 204*0 10024 8001 1000 13*0
  //   10024 8001 1000 13*0 10024 8001 1000 13*0 10024 8001 1000 13*0 10024 8001 1000 13*0 10024 8001 1000
  //   13*0 10024 8001 1000 13*0 10024 8001 1000 13*0 10024 8001 1000 13*0 10024 8001 1000 13*0 10024 8001
  //   1000 350*0 10024 8001 1000 13*0 10024 8001 1000 13*0 10024 8001 1000 13*0 10024 8001 1000 13*0 10024
  //   8001 1000 13*0 10024 8001 1000 13*0 10024 8001 1000 13*0 10024 8001 1000 13*0 10024 8001 1000 13*0
  //   10024 8001 1000 13*0 10024 8001 1000 1919*0 180000 31*0 180000 31*0 180000 31*0 180000 2427*0 200000
  //   contents of rom_2 (hex, n*v repeats v):
  //   1800c 1000000 14*0 1800c 1000000 14*0 1800c 1000000 14*0 1800c 1000000 14*0 1800c 1000000 14*0 1800c
  //   1000000 14*0 1800c 1000000 14*0 1800c 1000000 14*0 1800c 1000000 14*0 1800c 1000000 14*0 1800c
  //   1000000 14*0 1800c 1000000 14*0 1800c 1000000 14*0 1800c 1000000 14*0 1800c 1000000 14*0 1800c
  //   1000000 14*0 1800c 1000000 14*0 1800c 1000000 14*0 1800c 1000000 14*0 1800c 1000000 14*0 1800c
  //   1000000 14*0 1800c 1000000 14*0 1800c 1000000 14*0 1800c 1000000 14*0 1800c 1000000 14*0 1800c
  //   1000000 14*0 1800c 1000000 14*0 1800c 1000000 14*0 1800c 1000000 14*0 1800c 1000000 14*0 1800c
  //   1000000 14*0 1800c 1000000 14*0 1800c 1000000 14*0 1800c 1000000 14*0 1800c 1000000 14*0 1800c
  //   1000000 14*0 1800c 1000000 14*0 1800c 1000000 14*0 1800c 1000000 14*0 1800c 1000000 14*0 1800c
  //   1000000 14*0 1800c 1000000 14*0 1800c 1000000 14*0 1800c 1000000 14*0 1800c 1000000 14*0 1800c
  //   1000000 14*0 1800c 1000000 14*0 1800c 1000000 14*0 1800c 1000000 14*0 1800c 1000000 14*0 1800c
  //   1000000 14*0 1800c 1000000 14*0 1800c 1000000 14*0 1800c 1000000 14*0 1800c 1000000 14*0 1800c
  //   1000000 14*0 1800c 1000000 14*0 1800c 1000000 14*0 1800c 1000000 14*0 1800c 1000000 14*0 1800c
  //   1000000 14*0 1800c 1000000 14*0 1800c 1000000 4000000 13*0 1800c 1000000 2000000 13*0 1800c 1000000
  //   14*0 1800c 1000000 14*0 1800c 1000000 14*0 1800c 1000000 14*0 1800c 1000000 14*0 1800c 1000000 14*0
  //   1800c 1000000 14*0 1800c 1000000 14*0 1800c 1000000 14*0 1800c 1000000 14*0 1800c 1000000 14*0 1800c
  //   1000000 14*0 1800c 1000000 14*0 1800c 1000000 14*0 1800c 1000000 14*0 1800c 1000000 14*0 1800c
  //   1000000 14*0 1800c 1000000 14*0 1800c 1000000 14*0 1800c 1000000 14*0 1800c 1000000 14*0 1800c
  //   1000000 14*0 1800c 1000000 14*0 1800c 1000000 14*0 1800c 1000000 14*0 1800c 1000000 14*0 1800c
  //   1000000 14*0 1800c 1000000 14*0 1800c 1000000 14*0 1800c 1000000 14*0 1800c 1000000 14*0 1800c
  //   1000000 14*0 1800c 1000000 1800c 1000000 1800c 4010 10*0 1800c 1000000 1800c 1000000 28000 10 50000
  //   40 8*0 1800c 1000000 1000000 1000000 12*0 1800c 1000000 1000000 1000000 12*0 1800c 1000000 1000000
  //   1000000 12*0 1800c 1000000 1000000 1000000 12*0 1800c 1000000 1000000 1000000 12*0 1800c 1000000
  //   1000000 1000000 12*0 1800c 1000000 1000000 1000000 12*0 1800c 1000000 1000000 1000000 12*0 1800c
  //   1000000 14*0 1800c 1000000 14*0 1800c 1000000 14*0 1800c 1000000 14*0 1800c 1000000 1800c 1000000
  //   1800c 110000d 410080 10000d 408020 240 10000c00 110 4*0 1800c 1000000 20000c00 13*0 1800c 1000000
  //   10000d 400000 12*0 1800c 1000000 10000d 400000 12*0 1800c 1000000 10000d 400000 12*0 1800c 1000000
  //   10000d 400000 12*0 1800c 1000000 14*0 1800c 1000000 10000d 400000 12*0 1800c 1000000 800000 10000d
  //   12*0 1800c 1000000 800000 10000d 12*0 1800c 1000000 800000 10000d 12*0 1800c 1000000 800000 10000d
  //   12*0 1800c 1000000 800000 10000d 802100 10000d 4200 9*0 1800c 1000000 800000 10000d 12*0 1800c
  //   1000000 14*0 1800c 1000000 14*0 1800c 1000000 801800c 100200e 12*0 1800c 1000000 801800c 100200e
  //   12*0 1800c 1000000 1800c 1000000 12*0 1800c 1000000 1800c 1000000 12*0 1800c 1000000 1800c 1000000
  //   12*0 1800c 1000000 1800c 1000000 12*0 1800c 1000000 1800c 1000000 12*0 1800c 1000000 1800c 1000000
  //   12*0 1800c 1000000 1800c 1000000 2100 11*0 1800c 1000000 1800c 1000000 4200 11*0 1800c 1000000 14*0
  //   1800c 1000000 14*0 1800c 1000000 14*0 1800c 1000000 14*0 1800c 1000000 14*0 1800c 1000000 14*0 1800c
  //   1000000 14*0 1800c 1000000 14*0 1800c 1000000 801800c 1022000 801800c 100401c 10*0 1800c 1000000
  //   801800c 1022000 801800c 100401c 10*0 1800c 1000000 801800c 1022000 801800c 100401c 10*0 1800c
  //   1000000 801800c 1022000 801800c 100401c 10*0 1800c 1000000 801800c 1022000 801800c 100401c 10*0
  //   1800c 1000000 801800c 1022000 801800c 100401c 10*0 1800c 1000000 801800c 1022000 801800c 100401c
  //   10*0 1800c 1000000 801800c 1022000 801800c 100401c 10*0 1800c 1000000 801800c 1022000 801800c
  //   100401c 10*0 1800c 1000000 801800c 1022000 801800c 100401c 10*0 1800c 1000000 801800c 1022000
  //   801800c 100401c 10*0 1800c 1000000 801800c 1022000 801800c 100401c 10*0 1800c 1000000 14*0 1800c
  //   1000000 48 14 12*0 1800c 10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
  //   contents of rom_3 (hex, n*v repeats v):
  //   0 2000000 15*0 2000000 100000 4000000 13*0 2000000 80000 4000000 13*0 2000000 400000 4000000 13*0
  //   2000000 200000 4000000 13*0 2000000 10000 4000000 13*0 2000000 8000 4000000 13*0 2000000 40000
  //   4000000 13*0 2000000 20000 4000000 13*0 2000000 15*0 2000000 15*0 2000000 15*0 2000000 15*0 2000000
  //   15*0 2000000 15*0 2000000 15*0 2000000 0 4000000 13*0 2000000 0 4000000 13*0 2000000 0 4000000 13*0
  //   2000000 0 4000000 13*0 2000000 0 4000000 13*0 2000000 0 4000000 13*0 2000000 0 4000000 13*0 2000000
  //   0 4000000 13*0 2000000 0 4000000 13*0 2000000 0 4000000 13*0 2000000 0 4000000 13*0 2000000 0
  //   4000000 13*0 2000000 0 4000000 13*0 2000000 0 4000000 13*0 2000000 0 4000000 13*0 2000000 0 4000000
  //   13*0 2000000 15*0 2000000 15*0 2000000 15*0 2000000 15*0 2000000 15*0 2000000 15*0 2000000 15*0
  //   2000000 15*0 2000000 15*0 2000000 15*0 2000000 15*0 2000000 15*0 2000000 15*0 2000000 15*0 2000000
  //   15*0 2000000 15*0 2000000 0 0 81 4000000 11*0 2000000 0 0 101 4000000 11*0 2000000 0 0 201 4000000
  //   11*0 2000000 0 0 401 4000000 11*0 2000000 0 0 801 4000000 11*0 2000000 0 0 1001 4000000 11*0 2000000
  //   0 0 9 4000000 11*0 2000000 0 0 5 4000000 11*0 2000000 0 0 3 4000000 11*0 2000000 0 0 11 4000000 11*0
  //   2000000 0 0 21 4000000 11*0 2000000 15*0 2000000 0 41 4000000 12*0 2000000 0 41 4000000 12*0 2000000
  //   0 4000000 13*0 2000000 0 4000000 13*0 2000000 15*0 2000000 15*0 2000000 15*0 2000000 15*0 2000000
  //   15*0 2000000 15*0 2000000 15*0 2000000 15*0 2000000 15*0 2000000 15*0 2000000 15*0 2000000 15*0
  //   2000000 15*0 2000000 15*0 2000000 15*0 2000000 15*0 2000000 15*0 2000000 15*0 2000000 15*0 2000000
  //   15*0 2000000 15*0 2000000 15*0 2000000 15*0 2000000 15*0 2000000 15*0 2000000 15*0 2000000 15*0
  //   2000000 15*0 2000000 15*0 2000000 15*0 2000000 15*0 2000000 15*0 2000000 0 2000 0 80 4000000 10*0
  //   2000000 0 0 0 81 2000 100 4000000 8*0 2000000 0 0 4000000 12*0 2000000 0 0 4000000 12*0 2000000 0 0
  //   4000000 12*0 2000000 0 0 4000000 12*0 2000000 0 0 4000000 12*0 2000000 0 0 4000000 12*0 2000000 0 0
  //   4000000 12*0 2000000 0 0 4000000 12*0 2000000 15*0 2000000 15*0 2000000 15*0 2000000 15*0 2000000
  //   4*0 1000000 0 1000000 40 0 80 10000 4*0 2000000 10000 4000000 13*0 2000000 0 1000000 4000000 12*0
  //   2000000 0 1000000 4000000 12*0 2000000 0 1000000 4000000 12*0 2000000 0 1000000 4000000 12*0 2000000
  //   15*0 2000000 0 1000000 4000000 12*0 2000000 0 0 0 4000000 11*0 2000000 0 0 0 4000000 11*0 2000000 0
  //   0 0 4000000 11*0 2000000 0 0 0 4000000 11*0 2000000 5*0 4000000 9*0 2000000 0 0 8000000 4000000 11*0
  //   2000000 15*0 2000000 15*0 2000000 0 0 1800000 4000000 11*0 2000000 0 0 800000 0 4000000 10*0 2000000
  //   0 0 4000000 12*0 2000000 0 0 4000000 12*0 2000000 0 0 4000000 12*0 2000000 0 0 4000000 12*0 2000000
  //   0 0 4000000 12*0 2000000 0 8000000 4000000 12*0 2000000 0 0 0 4000000 11*0 2000000 0 0 0 4000000
  //   11*0 2000000 15*0 2000000 15*0 2000000 15*0 2000000 15*0 2000000 15*0 2000000 15*0 2000000 15*0
  //   2000000 15*0 2000000 0 2000 0 80 0 4000000 9*0 2000000 0 2000 0 80 0 4000000 9*0 2000000 0 2000 0 80
  //   0 4000000 9*0 2000000 0 2000 0 80 0 4000000 9*0 2000000 0 2000 0 80 1000000 4000000 9*0 2000000 0
  //   2000 0 80 1000000 4000000 9*0 2000000 0 2000 0 80 1000000 4000000 9*0 2000000 0 2000 0 80 1000000
  //   4000000 9*0 2000000 0 2000 0 80 0 4000000 9*0 2000000 0 2000 0 80 1000000 4000000 9*0 2000000 0 2000
  //   0 80 8000000 4000000 9*0 2000000 0 2000 0 80 1000000 4000000 9*0 2000000 15*0 2000000 0 0 0 4000000
  //   11*0 2000000 0 0 1000000 4000000 11*0 2000000 15*0 2000000 0 0 0 4000000 11*0 2000000 0 0 0 4000000
  //   11*0 2000000 0 0 0 4000000 11*0 2000000 0 0 0 4000000 11*0 2000000 0 0 1000000 4000000 11*0 2000000
  //   0 0 1000000 4000000 11*0 2000000 0 0 1000000 4000000 11*0 2000000 0 0 1000000 4000000 11*0 2000000 0
  //   0 8000000 4000000 11*0 2000000 0 0 0 4000000 11*0 2000000 0 0 1000000 4000000 11*0 2000000 0 0
  //   1000000 4000000 11*0 2000000 15*0 2000000 15*0 2000000 15*0 2000000 15*0 2000000 0 0 80 0 4000000
  //   10*0 2000000 0 0 80 0 4000000 10*0 2000000 0 0 80 1000000 4000000 10*0 2000000 0 0 80 1000000
  //   4000000 10*0 2000000 15*0 2000000 15*0 2000000 15*0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
endmodule

// PRE-DECODE
module PREDECODE__LOGIC (
  input  KOR,
  input  IRQ,
  input  CLK,
  input  DL_IR,
  input  RESCYC,
  input  RES,
  input  [7:0] FR,
  input  [7:0] DATA,
  output ADMEM,
  output INT,
  output [7:0] out_11,
  output [13:0] INST
);

  wire and_2_out, counter_1_carry, DIR_out, nor_1_out, nor_2_out, not_1_out, not_2_out, not_3_out, or_1_out,
       or_2_out, or_3_out, STACK_out, ZPG_out, ZPGI_out;

  Register IR (.D(DATA), .en(DL_IR), .Q(out_11), .clk(CLK), .clr(RES));
  not not_1 (not_1_out, or_2_out);
  not not_2 (not_2_out, CLK);
  or or_1 (or_1_out, RESCYC, RES, counter_1_carry);
  and and_1 (ADMEM, or_3_out, ~KOR, not_1_out);  // AND_Gate
  or or_2 (or_2_out, nor_2_out, nor_1_out);
  nor nor_1 (nor_1_out, INST[0], INST[1], INST[2], INST[3]);
  Counter #(.width(4), .max('hf)) counter_1 (
    .count(not_2_out), .Q(INST[3:0]), .carry(counter_1_carry), .clk(not_2_out), .clr(or_1_out));  // open: load, D
  and ZPGI (ZPGI_out, out_11[5], out_11[7], out_11[4]);
  or or_3 (or_3_out, ZPGI_out, ZPG_out, DIR_out, STACK_out);
  JUMP_decoder jump_decoder_1 (.OP(out_11), .ZF(FR[0]), .CF(FR[1]), .out_4(INST[12]));
  and and_2 (and_2_out, ~FR[6], ~FR[7], IRQ, nor_1_out);  // AND_Gate
  and ZPG (ZPG_out, out_11[5], out_11[7], ~out_11[4]);  // AND_Gate
  and DIR (DIR_out, ~out_11[5], out_11[7], out_11[4]);  // AND_Gate
  D_Flip_Flop d_ff_1 (.Q(INST[13]), .preset(and_2_out), .reset(or_1_out));  // open: clk, D, Qn, en
  nor nor_2 (nor_2_out, ~INST[0], INST[1], INST[2], INST[3]);  // NOR_Gate
  and STACK (STACK_out, ~out_11[7], out_11[6], out_11[5], out_11[4]);  // AND_Gate
  FLOWGATE flowgate_1 (
    .in_2(out_11[7]), .in_3(out_11[6]), .in_4(out_11[5]), .in_5(out_11[4]), .in_6(out_11[3]),
    .in_7(out_11[2]), .in_8(out_11[1]), .in_9(out_11[0]), .out_10(INST[11]), .out_11(INST[10]),
    .out_12(INST[9]), .out_13(INST[8]), .out_14(INST[7]), .out_15(INST[6]), .out_16(INST[5]),
    .out_17(INST[4]), .EN(not_3_out));
  not not_3 (not_3_out, INST[13]);

  assign INT = INST[13];

  // Notes on the sheet:
  //   INT TABLE
endmodule

module JUMP_decoder (
  input  [7:0] OP,
  input  ZF,
  input  CF,
  output out_4
);

  wire and_1_out, and_2_out, and_3_out, and_4_out, comparator_1_eq, comparator_2_eq, comparator_3_eq,
       comparator_4_eq, comparator_5_eq, comparator_6_eq, comparator_7_eq, comparator_8_eq, JC_out, JNC_out,
       JNZ_out, JZ_out;

  Comparator comparator_1 (.a(OP), .b(8'h62), .eq(comparator_1_eq));  // open: gt, lt
  Comparator comparator_2 (.a(OP), .b(8'h63), .eq(comparator_2_eq));  // open: gt, lt
  or JZ (JZ_out, comparator_2_eq, comparator_1_eq);
  and and_1 (and_1_out, JZ_out, ZF);
  Comparator comparator_3 (.a(OP), .b(8'h64), .eq(comparator_3_eq));  // open: gt, lt
  Comparator comparator_4 (.a(OP), .b(8'h65), .eq(comparator_4_eq));  // open: gt, lt
  or JNZ (JNZ_out, comparator_4_eq, comparator_3_eq);
  and and_2 (and_2_out, JNZ_out, ~ZF);  // AND_Gate
  Comparator comparator_5 (.a(OP), .b(8'h66), .eq(comparator_5_eq));  // open: gt, lt
  Comparator comparator_6 (.a(OP), .b(8'h67), .eq(comparator_6_eq));  // open: gt, lt
  or JC (JC_out, comparator_6_eq, comparator_5_eq);
  and and_3 (and_3_out, JC_out, CF);
  Comparator comparator_7 (.a(OP), .b(8'h68), .eq(comparator_7_eq));  // open: gt, lt
  Comparator comparator_8 (.a(OP), .b(8'h69), .eq(comparator_8_eq));  // open: gt, lt
  or JNC (JNC_out, comparator_8_eq, comparator_7_eq);
  and and_4 (and_4_out, JNC_out, ~CF);  // AND_Gate
  or or_1 (out_4, and_4_out, and_3_out, and_2_out, and_1_out);
endmodule

module PC (
  input  KF,
  input  IPC,
  input  [7:0] ADL,
  input  [7:0] ADH,
  input  CLK,
  input  ADL_UPCL,
  input  ADH_UPCH,
  input  ADL_KPCL,
  input  ADH_KPCH,
  input  PCL_ADL,
  input  PCH_ADH,
  input  ADL_PCL,
  input  ADH_PCH,
  input  in_14,
  output [7:0] ADL_2,
  output [7:0] ADH_2
);

  wire and_1_out, and_2_out, and_3_out, and_4_out, and_5_out, and_6_out, and_7_out, and_8_out, and_9_out,
       and_10_out, not_1_out, or_1_out, or_2_out, or_3_out, or_4_out, or_5_out, or_6_out, or_7_out, or_8_out,
       or_9_out, or_10_out;
  wire [7:0] controlled_buffer_1_out, controlled_buffer_2_out, controlled_buffer_3_out,
       controlled_buffer_4_out, KPCH_q, KPCL_q, multiplexer_1_out, multiplexer_2_out, UPCH_q, UPCL_q;
  wire [15:0] adder_1_out, adder_2_out;

  or or_1 (or_1_out, ADL_KPCL, and_6_out);
  or or_2 (or_2_out, and_3_out, ADL_UPCL);
  and and_1 (and_1_out, IPC, ~KF);  // AND_Gate
  assign controlled_buffer_1_out = or_1_out ? ADL : 8'bz;  // Controlled_Buffer controlled_buffer_1
  assign controlled_buffer_2_out = or_2_out ? ADL : 8'bz;  // Controlled_Buffer controlled_buffer_2
  assign controlled_buffer_3_out = or_3_out ? ADH : 8'bz;  // Controlled_Buffer controlled_buffer_3
  or or_3 (or_3_out, ADH_UPCH, and_2_out);
  assign controlled_buffer_4_out = or_4_out ? ADH : 8'bz;  // Controlled_Buffer controlled_buffer_4
  or or_4 (or_4_out, ADH_KPCH, and_7_out);
  or or_5 (or_5_out, ADL_UPCL, in_14);
  and and_2 (and_2_out, ADH_PCH, ~KF);  // AND_Gate
  and and_3 (and_3_out, ADL_PCL, ~KF);  // AND_Gate
  assign {controlled_buffer_3_out, controlled_buffer_2_out} = and_1_out ? adder_1_out : 16'bz;  // Controlled_Buffer controlled_buffer_5
  not not_1 (not_1_out, in_14);
  Multiplexer #(.width(8), .disabled(0), .enable("false")) multiplexer_1 (
    .in0(8'hf0), .in1(controlled_buffer_2_out), .out(multiplexer_1_out), .sel(not_1_out));
  or or_6 (or_6_out, and_1_out, and_3_out, or_5_out);
  Multiplexer #(.width(8), .disabled(0), .enable("false")) multiplexer_2 (
    .in0({8{1'b1}}), .in1(controlled_buffer_3_out), .out(multiplexer_2_out), .sel(not_1_out));
  or or_7 (or_7_out, and_1_out, and_2_out, or_8_out);
  or or_8 (or_8_out, ADH_UPCH, in_14);
  Register UPCL (.D(multiplexer_1_out), .en(or_6_out), .Q(UPCL_q), .clk(CLK));  // open: clr
  Register UPCH (.D(multiplexer_2_out), .en(or_7_out), .Q(UPCH_q), .clk(CLK));  // open: clr
  and and_4 (and_4_out, IPC, KF);
  Adder #(.width(16)) adder_1 (.a(16'h1), .b({UPCH_q, UPCL_q}), .out(adder_1_out));  // open: cin, cout
  or or_9 (or_9_out, and_4_out, and_6_out, ADL_KPCL);
  or or_10 (or_10_out, and_4_out, and_7_out, ADH_KPCH);
  assign ADL_2 = and_5_out ? UPCL_q : 8'bz;  // Controlled_Buffer controlled_buffer_6
  and and_5 (and_5_out, PCL_ADL, ~KF);  // AND_Gate
  and and_6 (and_6_out, ADL_PCL, KF);
  and and_7 (and_7_out, ADH_PCH, KF);
  assign {controlled_buffer_4_out, controlled_buffer_1_out} = and_4_out ? adder_2_out : 16'bz;  // Controlled_Buffer controlled_buffer_7
  assign ADL_2 = and_9_out ? KPCL_q : 8'bz;  // Controlled_Buffer controlled_buffer_8
  Register KPCL (.D(controlled_buffer_1_out), .en(or_9_out), .Q(KPCL_q), .clk(CLK));  // open: clr
  Register KPCH (.D(controlled_buffer_4_out), .en(or_10_out), .Q(KPCH_q), .clk(CLK));  // open: clr
  assign ADH_2 = and_8_out ? UPCH_q : 8'bz;  // Controlled_Buffer controlled_buffer_9
  and and_8 (and_8_out, PCH_ADH, ~KF);  // AND_Gate
  and and_9 (and_9_out, PCL_ADL, KF);
  Adder #(.width(16)) adder_2 (.a(16'h1), .b({KPCH_q, KPCL_q}), .out(adder_2_out));  // open: cin, cout
  assign ADH_2 = and_10_out ? KPCH_q : 8'bz;  // Controlled_Buffer controlled_buffer_10
  and and_10 (and_10_out, PCH_ADH, KF);

  // Notes on the sheet:
  //   RES
endmodule

module SP (
  input  ISP,
  input  DSP,
  input  [7:0] SB,
  input  [7:0] ADL,
  input  SP_ADL,
  input  CLK,
  input  in_7,
  input  SB_SP,
  input  SP_SB,
  input  ADL_SP,
  output [7:0] ADL_2,
  output [7:0] SB_2
);

  wire or_1_out, or_2_out, or_3_out;
  wire [7:0] controlled_buffer_1_out, counter_1_q;

  assign controlled_buffer_1_out = SB_SP ? SB : 8'bz;  // Controlled_Buffer controlled_buffer_1
  assign controlled_buffer_1_out = ADL_SP ? ADL : 8'bz;  // Controlled_Buffer controlled_buffer_2
  or or_1 (or_1_out, or_3_out, DSP);
  or or_2 (or_2_out, DSP, ISP);
  or or_3 (or_3_out, SB_SP, ADL_SP);
  Counter counter_1 (
    .load(or_1_out), .D(controlled_buffer_1_out), .count(or_2_out), .Q(counter_1_q), .clk(CLK), .clr(in_7));  // open: carry
  assign ADL_2 = SP_ADL ? counter_1_q : 8'bz;  // Controlled_Buffer controlled_buffer_3
  assign SB_2 = SP_SB ? counter_1_q : 8'bz;  // Controlled_Buffer controlled_buffer_4
endmodule

module CX (
  input  ICX,
  input  DCX,
  input  [7:0] SB,
  input  SB_CX,
  input  CLK,
  input  in_6,
  input  CX_ADL,
  input  CX_SB,
  output [7:0] ADL,
  output [7:0] SB_2
);

  wire or_1_out, or_2_out;
  wire [7:0] controlled_buffer_1_out, counter_1_q;

  assign controlled_buffer_1_out = SB_CX ? SB : 8'bz;  // Controlled_Buffer controlled_buffer_1
  or or_1 (or_1_out, SB_CX, DCX);
  or or_2 (or_2_out, DCX, ICX);
  Counter counter_1 (
    .load(or_1_out), .D(controlled_buffer_1_out), .count(or_2_out), .Q(counter_1_q), .clk(CLK), .clr(in_6));  // open: carry
  assign ADL = CX_ADL ? counter_1_q : 8'bz;  // Controlled_Buffer controlled_buffer_2
  assign SB_2 = CX_SB ? counter_1_q : 8'bz;  // Controlled_Buffer controlled_buffer_3
endmodule

module POINTER (
  input  ADL_PCL,
  input  ADH_PCH,
  input  DCX,
  input  ICX,
  input  DSP,
  input  ISP,
  input  IPC,
  input  [7:0] ADL,
  input  [7:0] ADH,
  input  [7:0] SB,
  input  ADL_UPCL,
  input  PCL_ADH,
  input  ADH_UPCH,
  input  PCH_ADH,
  input  ADL_KPCL,
  input  SP_ADL,
  input  ADH_KPCH,
  input  SP_SB,
  input  SB_SP,
  input  CX_ADL,
  input  ADL_SP,
  input  CX_SB,
  input  SB_CX,
  input  RES,
  input  KF,
  input  CLK,
  output [7:0] ADL_2,
  output [7:0] ADH_2,
  output [7:0] SB_2
);

  PC pc_1 (
    .KF(KF), .IPC(IPC), .ADL(ADL), .ADH(ADH), .ADL_UPCL(ADL_UPCL), .ADH_UPCH(ADH_UPCH), .ADL_KPCL(ADL_KPCL),
    .ADH_KPCH(ADH_KPCH), .PCL_ADL(PCL_ADH), .PCH_ADH(PCH_ADH), .ADL_2(ADL_2), .ADH_2(ADH_2), .CLK(CLK),
    .ADL_PCL(ADH_PCH), .ADH_PCH(ADL_PCL), .in_14(RES));
  SP sp_1 (
    .ISP(ISP), .DSP(DSP), .SB(SB), .ADL(ADL), .SB_SP(SB_SP), .ADL_SP(ADL_SP), .ADL_2(ADL_2), .SP_ADL(SP_ADL),
    .CLK(CLK), .SB_2(SB_2), .SP_SB(SP_SB), .in_7(RES));
  CX cx_1 (
    .ICX(ICX), .DCX(DCX), .SB(SB), .SB_CX(SB_CX), .ADL(ADL_2), .SB_2(SB_2), .CX_ADL(CX_ADL), .CX_SB(CX_SB),
    .CLK(CLK), .in_6(RES));
endmodule

module GATE (
  input  B_A,
  input  [7:0] B,
  input  [7:0] A,
  input  A_B,
  output [7:0] A_2,
  output [7:0] B_2
);

  assign A_2 = B_A ? B : 8'bz;  // Controlled_Buffer controlled_buffer_1
  assign B_2 = A_B ? A : 8'bz;  // Controlled_Buffer controlled_buffer_2
endmodule

module ADDRESS_BUS (
  input  ADDMEM,
  input  DEVICE,
  input  KF,
  input  R_nW,
  input  _1_ADH,
  input  _0_ADH,
  input  [7:0] ADL,
  input  [7:0] ADH,
  input  ADL_ABL,
  input  ADH_ABH,
  input  CLK,
  input  RES,
  output [17:0] AB
);

  wire [7:0] pull_resistor_1_node;

  Pull_Resistor pull_resistor_1 (.node(pull_resistor_1_node));
  assign ADH = _1_ADH ? 8'h1 : 8'bz;  // Controlled_Buffer controlled_buffer_1
  assign ADH = _0_ADH ? pull_resistor_1_node : 8'bz;  // Controlled_Buffer controlled_buffer_2
  Register register_1 (.D(ADL), .en(ADL_ABL), .Q(AB[7:0]), .clk(CLK), .clr(RES));
  Register register_2 (.D(ADH), .en(ADH_ABH), .Q(AB[15:8]), .clk(CLK), .clr(RES));
  and and_1 (AB[17], ~DEVICE, KF, ~ADDMEM, ~R_nW);  // AND_Gate

  assign AB[16] = DEVICE;
endmodule

module REGISTER (
  input  [7:0] SB,
  input  SB_AX,
  input  AX_SB,
  input  SB_BX,
  input  BX_SB,
  input  SB_DX,
  input  DX_SB,
  input  CLK,
  input  RES,
  output [7:0] out_10
);

  wire [7:0] AX_q, BX_q, DX_q;

  Register AX (.D(SB), .en(SB_AX), .Q(AX_q), .clk(CLK), .clr(RES));
  assign out_10 = AX_SB ? AX_q : 8'bz;  // Controlled_Buffer controlled_buffer_1
  Register BX (.D(SB), .en(SB_BX), .Q(BX_q), .clk(CLK), .clr(RES));
  assign out_10 = BX_SB ? BX_q : 8'bz;  // Controlled_Buffer controlled_buffer_2
  Register DX (.D(SB), .en(SB_DX), .Q(DX_q), .clk(CLK), .clr(RES));
  assign out_10 = DX_SB ? DX_q : 8'bz;  // Controlled_Buffer controlled_buffer_3
endmodule

module A_B (
  input  [7:0] DB,
  input  [7:0] SB,
  input  [7:0] ADL,
  input  [7:0] ADH,
  input  nDB_A,
  input  _0_A,
  input  DB_A,
  input  ADL_A,
  input  ADH_A,
  input  SB_B,
  input  _0_B,
  input  _1_B,
  input  CLK,
  input  RES,
  output [7:0] A,
  output [7:0] B
);

  wire or_1_out;
  wire [6:0] pull_resistor_2_node;
  wire [7:0] controlled_buffer_1_out, controlled_buffer_4_out, not_1_out, pull_resistor_1_node;

  assign not_1_out = ~DB;  // NOT_Gate not_1, 8 bits wide
  assign controlled_buffer_1_out = nDB_A ? not_1_out : 8'bz;  // Controlled_Buffer controlled_buffer_1
  Pull_Resistor pull_resistor_1 (.node(pull_resistor_1_node));
  Pull_Resistor pull_resistor_2 (.node(pull_resistor_2_node));
  or or_1 (or_1_out, _1_B, _0_B);
  assign controlled_buffer_1_out = _0_A ? pull_resistor_1_node : 8'bz;  // Controlled_Buffer controlled_buffer_2
  assign controlled_buffer_1_out = DB_A ? DB : 8'bz;  // Controlled_Buffer controlled_buffer_3
  assign controlled_buffer_4_out = SB_B ? SB : 8'bz;  // Controlled_Buffer controlled_buffer_4
  assign controlled_buffer_1_out = ADL_A ? ADL : 8'bz;  // Controlled_Buffer controlled_buffer_5
  assign controlled_buffer_4_out = or_1_out ? {pull_resistor_2_node, _1_B} : 8'bz;  // Controlled_Buffer controlled_buffer_6
  assign controlled_buffer_1_out = ADH_A ? ADH : 8'bz;  // Controlled_Buffer controlled_buffer_7
  Register u_A (.D(controlled_buffer_1_out), .Q(A), .clk(CLK), .clr(RES));  // open: en
  Register u_B (.D(controlled_buffer_4_out), .Q(B), .clk(CLK), .clr(RES));  // open: en
endmodule

module ALU (
  input  CF,
  input  [7:0] A,
  input  [7:0] B,
  input  ADD,
  input  ADC,
  input  SUB,
  input  SBB,
  input  MUL,
  input  DIV,
  input  SHL,
  input  SHR,
  input  AND,
  input  OR,
  input  XOR,
  input  NOT,
  output [7:0] SB,
  output ZERO,
  output COUT
);

  wire adder_1_cout, and_1_out, and_3_out, and_4_out, not_2_out, or_3_out, or_4_out, or_5_out, or_6_out,
       pull_resistor_2_node, subtractor_1_bout;
  wire [7:0] adder_1_out, and_2_out, divider_1_out, multiplier_1_out, not_1_out, or_2_out,
       pull_resistor_1_node, shifter_1_out, shifter_2_out, subtractor_1_out, xor_1_out;

  nor nor_1 (ZERO, pull_resistor_1_node[7], pull_resistor_1_node[6], pull_resistor_1_node[5], pull_resistor_1_node[4], pull_resistor_1_node[3], pull_resistor_1_node[2], pull_resistor_1_node[1], pull_resistor_1_node[0]);
  Pull_Resistor pull_resistor_1 (.node(pull_resistor_1_node));
  assign pull_resistor_1_node = SB;  // Buffer buffer_1, 8 bits wide
  Adder adder_1 (.a(A), .b(B), .out(adder_1_out), .cin(and_3_out), .cout(adder_1_cout));
  Subtractor subtractor_1 (.a(A), .b(B), .out(subtractor_1_out), .bin(and_3_out), .bout(subtractor_1_bout));
  and and_1 (and_1_out, subtractor_1_bout, or_5_out);
  Multiplier multiplier_1 (.a(A), .b(B), .out(multiplier_1_out));  // open: cin, cout
  or or_1 (COUT, and_1_out, and_4_out);
  Divider divider_1 (.a(A), .b(B), .out(divider_1_out));  // open: upper, rem
  Shifter shifter_1 (.in(A), .\dist (B[2:0]), .out(shifter_1_out));
  Shifter #(.shift("lr")) shifter_2 (.in(A), .\dist (B[2:0]), .out(shifter_2_out));
  assign and_2_out = A & B;  // AND_Gate and_2, 8 bits wide
  assign or_2_out = A | B;  // OR_Gate or_2, 8 bits wide
  assign xor_1_out = A ^ B;  // XOR_Gate xor_1, 8 bits wide
  assign not_1_out = ~A;  // NOT_Gate not_1, 8 bits wide
  or or_3 (or_3_out, ADC, SBB);
  and and_3 (and_3_out, CF, or_3_out);
  assign SB = or_4_out ? adder_1_out : 8'bz;  // Controlled_Buffer controlled_buffer_1
  assign SB = or_5_out ? subtractor_1_out : 8'bz;  // Controlled_Buffer controlled_buffer_2
  and and_4 (and_4_out, adder_1_cout, or_4_out);
  assign SB = MUL ? multiplier_1_out : 8'bz;  // Controlled_Buffer controlled_buffer_3
  assign SB = DIV ? divider_1_out : 8'bz;  // Controlled_Buffer controlled_buffer_4
  assign SB = SHL ? shifter_1_out : 8'bz;  // Controlled_Buffer controlled_buffer_5
  assign SB = SHR ? shifter_2_out : 8'bz;  // Controlled_Buffer controlled_buffer_6
  assign SB = AND ? and_2_out : 8'bz;  // Controlled_Buffer controlled_buffer_7
  assign SB = OR ? or_2_out : 8'bz;  // Controlled_Buffer controlled_buffer_8
  assign SB = XOR ? xor_1_out : 8'bz;  // Controlled_Buffer controlled_buffer_9
  assign SB = NOT ? not_1_out : 8'bz;  // Controlled_Buffer controlled_buffer_10
  or or_4 (or_4_out, ADD, ADC);
  or or_5 (or_5_out, SUB, SBB);
  or or_6 (or_6_out, or_4_out, or_5_out, MUL, DIV, SHL, SHR, AND, OR, XOR, NOT, pull_resistor_2_node);
  not not_2 (not_2_out, or_6_out);
  Pull_Resistor pull_resistor_2 (.node(pull_resistor_2_node));
endmodule

module DL (
  input  [7:0] DATA,
  input  DL_DB,
  input  DL_ADH,
  input  CLK,
  input  DL_ADL,
  input  DL_SB,
  output [7:0] out_7,
  output [7:0] SB,
  output [7:0] ADL,
  output [7:0] ADH,
  output [7:0] DB
);

  Register register_1 (.D(DATA), .en(CLK), .Q(out_7), .clk(CLK));  // open: clr
  assign SB = DL_SB ? out_7 : 8'bz;  // Controlled_Buffer controlled_buffer_1
  assign ADL = DL_ADL ? out_7 : 8'bz;  // Controlled_Buffer controlled_buffer_2
  assign ADH = DL_ADH ? out_7 : 8'bz;  // Controlled_Buffer controlled_buffer_3
  assign DB = DL_DB ? out_7 : 8'bz;  // Controlled_Buffer controlled_buffer_4
endmodule

module FR (
  input  CARRY,
  input  ZERO,
  input  DB_FR,
  input  ALUOP,
  input  [7:0] DB,
  input  FR_DB,
  input  CLZ,
  input  SEZ,
  input  CLC,
  input  SEC,
  input  CLK,
  input  SEK,
  input  CLI,
  input  SEI,
  input  CLK_2,
  input  RES,
  output [7:0] FR,
  output [7:0] DB_2,
  output ZF,
  output CF,
  output KF,
  output IF
);

  wire not_1_out, or_1_out, or_2_out, or_3_out, or_4_out, or_5_out, or_6_out, or_7_out;

  Pull_Resistor pull_resistor_1 (.node(DB));
  not not_1 (not_1_out, DB[6]);
  or or_1 (or_1_out, DB_FR, ALUOP);
  or or_2 (or_2_out, DB[0], ZERO);
  or or_3 (or_3_out, DB[1], CARRY);
  D_Flip_Flop d_ff_1 (.clk(CLK_2), .D(or_2_out), .Q(FR[0]), .preset(SEZ), .en(or_1_out), .reset(or_4_out));  // open: Qn
  D_Flip_Flop d_ff_2 (.clk(CLK_2), .D(or_3_out), .Q(CF), .preset(SEC), .en(or_1_out), .reset(or_5_out));  // open: Qn
  D_Flip_Flop d_ff_3 (.clk(CLK_2), .D(not_1_out), .Qn(FR[6]), .preset(or_6_out), .en(DB_FR), .reset(SEK));  // open: Q
  D_Flip_Flop d_ff_4 (.clk(CLK_2), .D(DB[7]), .Q(FR[7]), .preset(SEI), .en(DB_FR), .reset(or_7_out));  // open: Qn
  assign DB_2 = FR_DB ? {FR[7:5], {3{FR[5]}}, CF, FR[0]} : 8'bz;  // Controlled_Buffer controlled_buffer_1
  Pull_Resistor pull_resistor_2 (.node(FR[5]));
  or or_4 (or_4_out, RES, CLZ);
  or or_5 (or_5_out, RES, CLC);
  or or_6 (or_6_out, RES, CLK);
  or or_7 (or_7_out, RES, CLI);

  assign FR[4:1] = {{3{FR[5]}}, CF};
  assign IF = FR[7];
  assign KF = FR[6];
  assign ZF = FR[0];
endmodule

module R1 (
  input  [31:0] in_1,
  output out_2,
  output out_3,
  output out_4,
  output out_5,
  output out_6,
  output out_7,
  output out_8,
  output out_9,
  output out_10,
  output out_11,
  output out_12,
  output out_13,
  output out_14,
  output out_15,
  output out_16,
  output out_17,
  output out_18,
  output out_19,
  output out_20,
  output out_21,
  output out_22,
  output out_23,
  output out_24,
  output out_25,
  output out_26,
  output out_27,
  output out_28,
  output out_29,
  output out_30,
  output out_31,
  output out_32,
  output out_33
);


  assign out_2 = in_1[0];
  assign out_3 = in_1[1];
  assign out_4 = in_1[2];
  assign out_5 = in_1[3];
  assign out_6 = in_1[4];
  assign out_7 = in_1[5];
  assign out_8 = in_1[6];
  assign out_9 = in_1[7];
  assign out_10 = in_1[8];
  assign out_11 = in_1[9];
  assign out_12 = in_1[10];
  assign out_13 = in_1[11];
  assign out_14 = in_1[12];
  assign out_15 = in_1[13];
  assign out_16 = in_1[14];
  assign out_17 = in_1[15];
  assign out_18 = in_1[16];
  assign out_19 = in_1[17];
  assign out_20 = in_1[18];
  assign out_21 = in_1[19];
  assign out_22 = in_1[20];
  assign out_23 = in_1[21];
  assign out_24 = in_1[22];
  assign out_25 = in_1[23];
  assign out_26 = in_1[24];
  assign out_27 = in_1[25];
  assign out_28 = in_1[26];
  assign out_29 = in_1[27];
  assign out_30 = in_1[28];
  assign out_31 = in_1[29];
  assign out_32 = in_1[30];
  assign out_33 = in_1[31];
endmodule

module FLOWGATE (
  input  EN,
  input  in_2,
  input  in_3,
  input  in_4,
  input  in_5,
  input  in_6,
  input  in_7,
  input  in_8,
  input  in_9,
  output out_10,
  output out_11,
  output out_12,
  output out_13,
  output out_14,
  output out_15,
  output out_16,
  output out_17
);

  and and_1 (out_10, in_2, EN);
  and and_2 (out_11, in_3, EN);
  and and_3 (out_12, in_4, EN);
  and and_4 (out_13, in_5, EN);
  and and_5 (out_14, in_6, EN);
  and and_6 (out_15, in_7, EN);
  and and_7 (out_16, in_8, EN);
  and and_8 (out_17, in_9, EN);
endmodule

// VEC-TABLE
module VECTOR_TABLE (
  input  CALLVEC,
  input  RETVEC,
  input  INTVEC,
  output [7:0] ADL,
  output [7:0] ADH
);

  wire or_1_out;

  or or_1 (or_1_out, RETVEC, CALLVEC);
  assign ADL = CALLVEC ? 8'ha0 : 8'bz;  // Controlled_Buffer controlled_buffer_1
  assign ADL = RETVEC ? 8'hb0 : 8'bz;  // Controlled_Buffer controlled_buffer_2
  assign ADH = INTVEC ? 8'hfe : 8'bz;  // Controlled_Buffer controlled_buffer_3
  assign ADH = or_1_out ? {8{1'b1}} : 8'bz;  // Controlled_Buffer controlled_buffer_4
endmodule

module KEYBOARD (
  input  BUFFER,
  input  [6:0] DATA,
  input  CLK,
  input  DEV,
  input  R_W,
  input  [7:0] ADDRESS,
  input  INT,
  output KCLK,
  output IRQ,
  output [7:0] DATA_2
);

  wire and_1_out, and_2_out, comparator_1_eq, d_ff_1_q, pull_resistor_2_node;
  wire [7:7] pull_resistor_1_node;

  Comparator comparator_1 (.a(ADDRESS), .b(8'ha0), .eq(comparator_1_eq));  // open: gt, lt
  and and_1 (and_1_out, INT, BUFFER);
  and and_2 (and_2_out, DEV, comparator_1_eq, ~R_W);  // AND_Gate
  assign DATA_2 = and_1_out ? 8'ha0 : 8'bz;  // Controlled_Buffer controlled_buffer_1
  D_Flip_Flop d_ff_1 (.clk(CLK), .D(and_2_out), .Q(d_ff_1_q));  // open: Qn, preset, en, reset
  Pull_Resistor pull_resistor_1 (.node(pull_resistor_1_node[7]));
  assign DATA_2 = and_2_out ? {pull_resistor_1_node[7], DATA} : 8'bz;  // Controlled_Buffer controlled_buffer_2
  D_Flip_Flop d_ff_2 (.clk(CLK), .D(d_ff_1_q), .Q(KCLK));  // open: Qn, preset, en, reset
  Pull_Resistor #(.pull(1)) pull_resistor_2 (.node(pull_resistor_2_node));
  assign IRQ = BUFFER ? pull_resistor_2_node : 1'bz;  // Controlled_Buffer controlled_buffer_3
endmodule

module MEMORY (
  input  [7:0] DATA_IN,
  input  [17:0] AB,
  input  CLK,
  input  R_W,
  output [7:0] DATA_OUT
);

  wire nor_1_out, not_1_out, not_2_out;
  wire [7:0] controlled_buffer_2_out;

  assign DATA_OUT = not_1_out ? controlled_buffer_2_out : 8'bz;  // Controlled_Buffer controlled_buffer_1
  assign controlled_buffer_2_out = R_W ? DATA_IN : 8'bz;  // Controlled_Buffer controlled_buffer_2
  not not_1 (not_1_out, R_W);
  nor nor_1 (nor_1_out, AB[16], AB[17]);
  not not_2 (not_2_out, R_W);
  RAM #(.addrWidth(16)) ram_1 (
    .addr(AB[15:0]), .data(controlled_buffer_2_out), .sel(nor_1_out), .clk(CLK), .ld(not_2_out));  // open: clr
  ROM #(.addrWidth(16)) rom_1 (.addr(AB[15:0]), .data(controlled_buffer_2_out), .sel(AB[17]));

  // Notes on the sheet:
  //   contents of rom_1 (hex, n*v repeats v):
  //   2 4 8 84 ff 86 0 87 2 6 65174*0 7f a0 6 253*0 70 71 72 73 75 6 10*0 7b 79 78 77 76 7a 6
endmodule

module Terminal_Controller (
  input  DEVICE,
  input  [7:0] Address,
  input  R_W,
  input  CLK,
  input  [7:0] Data,
  output CLK_TERM,
  output [6:0] DATA_2,
  output CLS
);

  wire and_1_out, comparator_1_eq, pull_resistor_1_node;

  and and_1 (and_1_out, Data[7], Data[6], Data[5], Data[4], Data[3], Data[2], Data[1], Data[0], pull_resistor_1_node);
  Comparator comparator_1 (.a(Address), .b(8'hc0), .eq(comparator_1_eq));  // open: gt, lt
  and and_2 (CLK_TERM, DEVICE, comparator_1_eq, R_W, CLK);
  Bit_Extender #(.out_width(7)) bit_extender_1 (.in(Data), .out(DATA_2));
  Pull_Resistor #(.pull(1)) pull_resistor_1 (.node(pull_resistor_1_node));
  and and_3 (CLS, CLK_TERM, and_1_out);
endmodule

module EXTERNAL_MEMORY (
  input  [7:0] D,
  input  CLK,
  input  DEVICE,
  input  R_W,
  input  [7:0] Address,
  output [7:0] Q
);

  wire and_1_out, comparator_1_eq, comparator_2_eq, comparator_3_eq, not_1_out, not_2_out;
  wire [7:0] controlled_buffer_1_out, controlled_buffer_3_out, register_1_q, register_2_q;

  assign controlled_buffer_1_out = DEVICE ? Address : 8'bz;  // Controlled_Buffer controlled_buffer_1
  Pull_Resistor pull_resistor_1 (.node(controlled_buffer_1_out));
  assign Q = not_1_out ? controlled_buffer_3_out : 8'bz;  // Controlled_Buffer controlled_buffer_2
  assign controlled_buffer_3_out = and_1_out ? D : 8'bz;  // Controlled_Buffer controlled_buffer_3
  and and_1 (and_1_out, R_W, comparator_1_eq);
  Register register_1 (.D(D), .en(comparator_2_eq), .Q(register_1_q), .clk(CLK));  // open: clr
  Register register_2 (.D(D), .en(comparator_3_eq), .Q(register_2_q), .clk(CLK));  // open: clr
  Comparator #(.mode("unsigned")) comparator_1 (
    .a(controlled_buffer_1_out), .b(8'hd0), .eq(comparator_1_eq));  // open: gt, lt
  Comparator #(.mode("unsigned")) comparator_2 (
    .a(controlled_buffer_1_out), .b(8'hd1), .eq(comparator_2_eq));  // open: gt, lt
  Comparator #(.mode("unsigned")) comparator_3 (
    .a(controlled_buffer_1_out), .b(8'hd2), .eq(comparator_3_eq));  // open: gt, lt
  not not_1 (not_1_out, and_1_out);
  not not_2 (not_2_out, R_W);
  RAM #(.addrWidth(16)) ram_1 (
    .addr({register_2_q, register_1_q}), .data(controlled_buffer_3_out), .sel(comparator_1_eq), .clk(CLK),
    .ld(not_2_out));  // open: clr
endmodule
